# Fritzing sketch 8th_MFB (saved by Fritzing 0.9.3b)
breadboards: 1

parts:
  IC1 = Dual Op-Amp [package=dip08]
  IC2 = Dual Op-Amp [package=dip08]
  C1 = Ceramic Capacitor [capacitance=100nF package="100 mil [THT, multilayer]"]
  C2 = Ceramic Capacitor [capacitance=100nF package="100 mil [THT, multilayer]"]
  R1 = Resistor [tolerance=±5% resistance=8.2k package=THT]
  R2 = Resistor [tolerance=±5% resistance=4.7k package=THT]
  R4 = Resistor [tolerance=±5% resistance=10k package=THT]
  R5 = Resistor [tolerance=±5% resistance=4.7k package=THT]
  R6 = Resistor [tolerance=±5% resistance=4.7k package=THT]
  R7 = Resistor [tolerance=±5% resistance=4.7k package=THT]
  C7 = Film/Foil Capacitor [capacitance=100nF voltage=35V package="5mm [THT, pp]"]
  C8 = Film/Foil Capacitor [capacitance=100nF voltage=35V package="5mm [THT, pp]"]
  C9 = Film/Foil Capacitor [capacitance=100nF voltage=35V package="5mm [THT, pp]"]
  C11 = Film/Foil Capacitor [capacitance=100nF voltage=35V package="5mm [THT, pp]"]
  C12 = Ceramic Capacitor [capacitance=100nF package="100 mil [THT, multilayer]"]
  C13 = Ceramic Capacitor [capacitance=100nF package="100 mil [THT, multilayer]"]
  C14 = Film/Foil Capacitor [capacitance=100nF voltage=35V package="5mm [THT, pp]"]
  R8 = Resistor [tolerance=±5% resistance=3.3k package=THT]
  R9 = Resistor [tolerance=±5% resistance=15k package=THT]
  R10 = Resistor [tolerance=±5% resistance=3.3k package=THT]
  C15 = Film/Foil Capacitor [capacitance=100nF voltage=35V package="5mm [THT, pp]"]
  C16 = Film/Foil Capacitor [capacitance=100nF voltage=35V package="5mm [THT, pp]"]
  R11 = Resistor [tolerance=±5% resistance=3.9k package=THT]
  R12 = Resistor [tolerance=±5% resistance=15k package=THT]
  R13 = Resistor [tolerance=±5% resistance=3.9k package=THT]
  C17 = Film/Foil Capacitor [capacitance=100nF voltage=35V package="5mm [THT, pp]"]
  C18 = Electrolytic Capacitor [capacitance=1µF package="100 mil [THT, electrolytic]"]
  C19 = Electrolytic Capacitor [capacitance=1µF package="100 mil [THT, electrolytic]"]
  U1 = mystery part, 3 pins [chip_label=TLE2426]
  C20 = Electrolytic Capacitor [capacitance=1µF package="100 mil [THT, electrolytic]"]
  VCC1 = Battery block 9V

nets:
  N1: IC1.A_OUT, R10.Pin_1, C16.-, R11.Pin_0
  N2: IC1.A_-IN, C16.+, R12.Pin_0
  N3: IC1.A_+IN, IC1.B_+IN, IC2.A_+IN, IC2.B_+IN, C1.0, C2.0, C7.+, C9.-, C12.0, C13.0, C15.-, C17.+, C18.+, C19.+, U1.pin1
  N4: IC1.A_V-, IC2.A_V-, C1.1, C13.1, C19.-, U1.pin2, C20.-, VCC1.-
  N5: IC1.B_-IN, C14.-, R9.Pin_0
  N6: IC1.B_OUT, C14.+, R8.Pin_0
  N7: IC1.A_V+, IC2.A_V+, C2.1, C12.1, C18.-, U1.pin3, C20.+, VCC1.+
  N8: IC2.A_OUT, R5.Pin_1, R7.Pin_0, C8.-
  N9: IC2.A_-IN, R1.Pin_0, C8.+
  N10: IC2.B_-IN, R4.Pin_0, C11.-
  N11: IC2.B_OUT, R6.Pin_0, C11.+, R13.Pin_1
  N12: R1.Pin_1, R2.Pin_0, R7.Pin_1, C7.-
  N13: R4.Pin_1, R5.Pin_0, R6.Pin_1, C9.+
  N14: R8.Pin_1, R9.Pin_1, R10.Pin_0, C15.+
  N15: R11.Pin_1, R12.Pin_1, R13.Pin_0, C17.-

notes:
  IN
  OUT
  VEE
  GND
  GND
  VCC
